# Fritzing sketch fig04 (saved by Fritzing 0.9.6b)
breadboards: 1

parts:
  Raspberry_Pi_1 = Raspberry Pi 3 [part_number=RPI-3-V1.2]
  Componente1 = Real Time Clock Module - DS1307 RTC Breakout Board
  TC1 = DIP - 8 pins [chip_label=TC74 package="DIP (Dual Inline) [THT]"]

nets:
  N1: Raspberry_Pi_1.GPIO2, Componente1.SDA, TC1.pin2
  N2: Raspberry_Pi_1.GPIO3, Componente1.SCL, TC1.pin3
  GND: Raspberry_Pi_1.GND, Componente1.GND, TC1.pin8
  5V: Raspberry_Pi_1.5V, Componente1.5V, TC1.pin1

custom parts:
  DIP - 8 pins: A DIP stand-in part for whatever IC you want. With 8 pins on a 300mil dual inline package (DIP) footprint.
